# Fritzing sketch LXF316 (saved by Fritzing 0.9.8b)

parts:
  Mod1 = Raspberry Pi Pico
  Part1 = LCD1602-I2C

nets:
  N1: Mod1.pin_1, Part1.SDA
  N2: Mod1.pin_2, Part1.SCL
  N3: Mod1.pin_33, Mod1.pin_38, Part1.GND
  N4: Mod1.pin_40, Part1.VCC

custom parts:
  Raspberry Pi Pico: Raspberry Pi Pico. Based around the RP2040 microcontroller the Pico is a low cost microcontroller device bringing Raspberry Pi quality, cost, and easy of use to the microcontroller space. Jan 2021, Split part in to two versions: tht (this one) and SMD. This one will drill holes for a .1 in header in pcb to allow plugging in the module as well as providing pads to solder the module to the top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
  LCD1602-I2C: A standard character display, usually with 2x16 characters. Comes in many colors with LCM1602 IIC attached.
